// Logisim project SAP-1.circ as structural Verilog: 7 circuits, main circuit main
module main (
  input  CLK
);

  wire ringcounter_1_t1, ringcounter_1_t2, ringcounter_1_t3, ringcounter_1_t4, ringcounter_1_t5,
       ringcounter_1_t6;

  RingCounter ringcounter_1 (
    .CLK(CLK), .T1(ringcounter_1_t1), .T2(ringcounter_1_t2), .T3(ringcounter_1_t3), .T4(ringcounter_1_t4),
    .T5(ringcounter_1_t5), .T6(ringcounter_1_t6));
endmodule

module ProgramCounter (
  input  Cp,
  input  nCLK,
  input  CLR,
  input  Ep,
  output [3:0] OUT_BUS
);

  wire adder_1_cout, adder_1_out, adder_2_cout, adder_2_out, adder_3_cout, adder_3_out, adder_4_out,
       not_1_out;
  wire [3:0] d_ff_1_q;

  not not_1 (not_1_out, nCLK);
  D_Flip_Flop d_ff_1 (.clk(not_1_out), .D(adder_1_out), .Q(d_ff_1_q[0]), .reset(CLR));  // open: Qn, preset, en
  Adder #(.width(1)) adder_1 (.a(Cp), .b(d_ff_1_q[0]), .out(adder_1_out), .cout(adder_1_cout));  // open: cin
  D_Flip_Flop d_ff_2 (.clk(not_1_out), .D(adder_2_out), .Q(d_ff_1_q[1]), .reset(CLR));  // open: Qn, preset, en
  D_Flip_Flop d_ff_3 (.clk(not_1_out), .D(adder_3_out), .Q(d_ff_1_q[2]), .reset(CLR));  // open: Qn, preset, en
  Adder #(.width(1)) adder_2 (.a(adder_1_cout), .b(d_ff_1_q[1]), .out(adder_2_out), .cout(adder_2_cout));  // open: cin
  D_Flip_Flop d_ff_4 (.clk(not_1_out), .D(adder_4_out), .Q(d_ff_1_q[3]), .reset(CLR));  // open: Qn, preset, en
  Adder #(.width(1)) adder_3 (.a(adder_2_cout), .b(d_ff_1_q[2]), .out(adder_3_out), .cout(adder_3_cout));  // open: cin
  assign OUT_BUS = Ep ? d_ff_1_q : 4'bz;  // Controlled_Buffer controlled_buffer_1
  Adder #(.width(1)) adder_4 (.a(adder_3_cout), .b(d_ff_1_q[3]), .out(adder_4_out));  // open: cin, cout
endmodule

module MemoryAddressRegister (
  input  CLK,
  input  [3:0] IN_BUS,
  input  nLm,
  input  CLR,
  output [3:0] OUT_RAM
);

  wire [3:0] controlled_buffer_1_out;

  assign controlled_buffer_1_out = nLm ? IN_BUS : 4'bz;  // Controlled_Buffer controlled_buffer_1
  D_Flip_Flop d_ff_1 (.clk(CLK), .D(controlled_buffer_1_out[0]), .Q(OUT_RAM[0]), .reset(CLR));  // open: Qn, preset, en
  D_Flip_Flop d_ff_2 (.clk(CLK), .D(controlled_buffer_1_out[1]), .Q(OUT_RAM[1]), .reset(CLR));  // open: Qn, preset, en
  D_Flip_Flop d_ff_3 (.clk(CLK), .D(controlled_buffer_1_out[2]), .Q(OUT_RAM[2]), .reset(CLR));  // open: Qn, preset, en
  D_Flip_Flop d_ff_4 (.clk(CLK), .D(controlled_buffer_1_out[3]), .Q(OUT_RAM[3]), .reset(CLR));  // open: Qn, preset, en
endmodule

module RAM (
  input  [3:0] Address,
  input  [7:0] Data,
  input  nCE,
  output [7:0] OUT_BUS
);

  wire not_1_out;

  not not_1 (not_1_out, nCE);
  RAM_part #(.addrWidth(4), .bus("separate")) ram_1 (
    .addr(Address), .din(Data), .data(OUT_BUS), .ld(not_1_out));  // open: str, sel, clk, clr
endmodule

module InstructionRegister (
  input  nEi,
  input  CLK,
  input  CLR,
  input  [7:0] IN_BUS,
  input  nLi,
  output [3:0] OUT_BUS,
  output [3:0] OUT_CTRL
);

  wire [3:0] d_ff_2_q;
  wire [7:0] controlled_buffer_1_out;

  assign controlled_buffer_1_out = nLi ? IN_BUS : 8'bz;  // Controlled_Buffer controlled_buffer_1
  D_Flip_Flop d_ff_1 (.clk(CLK), .D(controlled_buffer_1_out[1]), .Q(d_ff_2_q[1]), .reset(CLR));  // open: Qn, preset, en
  D_Flip_Flop d_ff_2 (.clk(CLK), .D(controlled_buffer_1_out[0]), .Q(d_ff_2_q[0]), .reset(CLR));  // open: Qn, preset, en
  D_Flip_Flop d_ff_3 (.clk(CLK), .D(controlled_buffer_1_out[2]), .Q(d_ff_2_q[2]), .reset(CLR));  // open: Qn, preset, en
  D_Flip_Flop d_ff_4 (
    .clk(CLK), .D(controlled_buffer_1_out[3]), .Q(d_ff_2_q[3]), .en(CLR), .reset(CLR));  // open: Qn, preset
  D_Flip_Flop d_ff_5 (.clk(CLK), .D(controlled_buffer_1_out[4]), .Q(OUT_CTRL[0]), .reset(CLR));  // open: Qn, preset, en
  assign OUT_BUS = nEi ? d_ff_2_q : 4'bz;  // Controlled_Buffer controlled_buffer_2
  D_Flip_Flop d_ff_6 (.clk(CLK), .D(controlled_buffer_1_out[5]), .Q(OUT_CTRL[1]), .reset(CLR));  // open: Qn, preset, en
  D_Flip_Flop d_ff_7 (.clk(CLK), .D(controlled_buffer_1_out[6]), .Q(OUT_CTRL[2]), .reset(CLR));  // open: Qn, preset, en
  D_Flip_Flop d_ff_8 (.clk(CLK), .D(controlled_buffer_1_out[7]), .Q(OUT_CTRL[3]), .reset(CLR));  // open: Qn, preset, en
endmodule

module RingCounter (
  input  CLK,
  output T1,
  output T2,
  output T3,
  output T4,
  output T5,
  output T6
);

  wire nor_1_out;

  nor nor_1 (nor_1_out, T1, T2, T3, T4, T5, T6);
  D_Flip_Flop d_ff_1 (.clk(CLK), .D(nor_1_out), .Q(T1));  // open: Qn, preset, en, reset
  D_Flip_Flop d_ff_2 (.clk(CLK), .D(T1), .Q(T2));  // open: Qn, preset, en, reset
  D_Flip_Flop d_ff_3 (.clk(CLK), .D(T2), .Q(T3));  // open: Qn, preset, en, reset
  D_Flip_Flop d_ff_4 (.clk(CLK), .D(T3), .Q(T4));  // open: Qn, preset, en, reset
  D_Flip_Flop d_ff_5 (.clk(CLK), .D(T4), .Q(T5));  // open: Qn, preset, en, reset
  D_Flip_Flop d_ff_6 (.clk(CLK), .D(T5), .Q(T6));  // open: Qn, preset, en, reset
endmodule

module Instruction_Decoder (
  input  I4,
  input  I5,
  input  I6,
  input  I7,
  output LDA,
  output ADD,
  output SUB,
  output OUT,
  output HLT
);

  wire not_1_out, not_2_out, not_3_out, not_4_out, not_5_out, not_6_out, not_7_out, not_8_out, not_9_out;

  not not_1 (not_1_out, I5);
  not not_2 (not_2_out, I6);
  not not_3 (not_3_out, I7);
  not not_4 (not_4_out, I4);
  not not_5 (not_5_out, I6);
  not not_6 (not_6_out, I7);
  not not_7 (not_7_out, I6);
  not not_8 (not_8_out, I7);
  not not_9 (not_9_out, I7);
  and and_1 (LDA, I4, not_1_out, not_2_out, not_3_out);
  and and_2 (ADD, not_4_out, I5, not_5_out, not_6_out);
  and and_3 (SUB, I4, I5, not_7_out, not_8_out);
  and and_4 (OUT, I4, I5, I6, not_9_out);
  and and_5 (HLT, I4, I5, I6, I7);

  // Notes on the sheet:
  //   LDA - 0001
  //   ADD - 0010
  //   SUB - 0011
  //   OUT - 0111
  //   HLT - 1111
  //   N/A - anything else
endmodule
